# Fritzing sketch Teensy-Theremin5 -3 (saved by Fritzing 0.9.0b)
circuit board: 9.02587cm x 9.05239cm
breadboards: 2

parts:
  LDR = Photocell (LDR) [package=THT]
  R2 = Resistor [tolerance=±5% resistance=10k package=THT]
  U1 = POT [package=pot_mammoth]
  U2 = POT [package=pot_mammoth]
  S2 = Round Pushbutton
  S3 = Round Pushbutton
  S4 = Round Pushbutton
  S5 = Round Pushbutton
  U3 = POT [package=pot_mammoth]
  U4 = POT [package=pot_mammoth]
  R7 = Resistor [tolerance=±5% resistance=10k package=THT]
  R8 = Resistor [tolerance=±5% resistance=10k package=THT]
  R10 = Resistor [tolerance=±5% resistance=10k package=THT]
  R9 = Resistor [tolerance=±5% resistance=10k package=THT]
  J1 = female pin header, 14 pins [form="♀ (female)"]
  J2 = female pin header, 14 pins [form="♀ (female)"]
  HC-SR04 = female pin header, 4 pins [form="♀ (female)"]

nets:
  N1: LDR.pin_0, R2.Pin_1, J1.pin7
  N2: LDR.pin_1, U1.E, U2.E, S2.leg1, S3.leg1, S4.leg1, S5.leg1, U3.E, U4.E, J1.pin3
  N3: R2.Pin_0, U1.S, U2.S, U3.S, U4.S, R7.Pin_1, R8.Pin_1, R10.Pin_1, R9.Pin_1, J2.pin1, HC-SR04.pin4
  N4: U1.A, J1.pin6
  N5: U2.A, J1.pin10
  N6: S2.leg0, R7.Pin_0, J2.pin4
  N7: S3.leg0, R8.Pin_0, J2.pin5
  N8: S4.leg0, R9.Pin_0, J2.pin6
  N9: S5.leg0, R10.Pin_0, J2.pin7
  N10: U3.A, J1.pin11
  N11: U4.A, J1.pin12
  N12: J1.pin1, HC-SR04.pin1
  N13: J2.pin2, HC-SR04.pin2
  N14: J2.pin3, HC-SR04.pin3

notes:
  KonkaSynth
